# Fritzing sketch chameleon_glove (saved by Fritzing 0.7.5b)

parts:
  FLORA = Adafruit_Flora
  Index_Finger = Neopixel Strip -- Black (60/m)
  Neopixel_Ring = Neopixel Ring 16
  Middle_Finger = Neopixel Strip -- Black (60/m)
  Ring_Finger = Neopixel Strip -- Black (60/m)
  Pinky = Neopixel Strip -- Black (60/m)
  Thumb = Neopixel Strip -- Black (60/m)
  Color_Sensor = FLORA Color Sensor
  Compass = Flora Accelerometer/Compass Sensor
  Tactile_mode_switch = Pushbutton [package=THT]
  Velcro_ON_button = Pushbutton [package=THT]
  Color_sensor_switch = Pushbutton [package=THT]
  Battery = LiPoly Battery (1300mAh)

nets:
  GND: FLORA.connector1, Color_Sensor.GND, Compass.GND, Color_sensor_switch.leg1
  N1: FLORA.connector2, Compass.SCL#2
  N2: FLORA.connector3, Compass.SDA#3
  N3: FLORA.connector4, Color_Sensor.3V, Compass.3V3
  GND_2: FLORA.connector7, Index_Finger.GND, Neopixel_Ring.GND, Middle_Finger.GND, Ring_Finger.GND, Pinky.GND, Thumb.GND, Battery.negative
  +5V: FLORA.connector8, Index_Finger.+5V, Neopixel_Ring.VCC, Middle_Finger.+5V, Ring_Finger.+5V, Pinky.+5V, Thumb.+5V, Battery.positive
  N4: FLORA.connector9, Velcro_ON_button.leg1
  N5: FLORA.connector10, Tactile_mode_switch.leg1
  N6: FLORA.connector11, Tactile_mode_switch.leg0, Velcro_ON_button.leg0
  N7: FLORA.connector12, Neopixel_Ring.IN
  N8: FLORA.connector13, Color_sensor_switch.leg0
  N9: Index_Finger.DI, Neopixel_Ring.OUT
  N10: Index_Finger.DO, Middle_Finger.DI
  N11: Middle_Finger.DO, Ring_Finger.DI
  N12: Ring_Finger.DO, Pinky.DI
  N13: Pinky.DO, Thumb.DI
  N14: Color_Sensor.SCL, Compass.SCL#6
  N15: Color_Sensor.SDA, Compass.SDA#5

custom parts:
  Neopixel Strip -- Black (60/m): Neopixel Strip, Black, 60 pixels per meter.
  Neopixel Ring 16: Neopixel Ring x16
  FLORA Color Sensor: Adafruit FLORA Color Sensor with TCS34725
  Flora Accelerometer/Compass Sensor: Flora Accelerometer and Compass Sensor - LSM303
  LiPoly Battery (1300mAh): Lithium Ion Polymer Battery (1300mAh)
