# Fritzing sketch chameleon_glove_basic (saved by Fritzing 0.7.5b)

parts:
  FLORA = Adafruit_Flora
  Index_Finger = Neopixel Strip -- Black (60/m)
  Middle_Finger = Neopixel Strip -- Black (60/m)
  Ring_Finger = Neopixel Strip -- Black (60/m)
  Pinky = Neopixel Strip -- Black (60/m)
  Thumb = Neopixel Strip -- Black (60/m)
  Color_Sensor = FLORA Color Sensor
  Color_sensor_switch = Pushbutton [package=THT]
  Battery = LiPoly Battery (1300mAh)
  Neopixel_Ring = Neopixel Ring 16

nets:
  N1: FLORA.connector1, Color_Sensor.GND, Color_sensor_switch.leg1
  N2: FLORA.connector2, Color_Sensor.SCL
  N3: FLORA.connector3, Color_Sensor.SDA
  N4: FLORA.connector4, Color_Sensor.3V
  GND: FLORA.connector7, Index_Finger.GND, Middle_Finger.GND, Ring_Finger.GND, Pinky.GND, Thumb.GND, Battery.negative, Neopixel_Ring.GND
  +5V: FLORA.connector8, Index_Finger.+5V, Middle_Finger.+5V, Ring_Finger.+5V, Pinky.+5V, Thumb.+5V, Battery.positive, Neopixel_Ring.VCC
  N5: FLORA.connector12, Neopixel_Ring.IN
  N6: FLORA.connector13, Color_sensor_switch.leg0
  N7: Index_Finger.DI, Neopixel_Ring.OUT
  N8: Index_Finger.DO, Middle_Finger.DI
  N9: Middle_Finger.DO, Ring_Finger.DI
  N10: Ring_Finger.DO, Pinky.DI
  N11: Pinky.DO, Thumb.DI

custom parts:
  Neopixel Strip -- Black (60/m): Neopixel Strip, Black, 60 pixels per meter.
  FLORA Color Sensor: Adafruit FLORA Color Sensor with TCS34725
  LiPoly Battery (1300mAh): Lithium Ion Polymer Battery (1300mAh)
  Neopixel Ring 16: Neopixel Ring x16
